# Fritzing sketch PlantMonitor (saved by Fritzing 0.9.6b)
breadboards: 1

parts:
  U1 = NodeMCU V1.0
  OLED1 = 128x32 I2C Monochrome OLED Display
  DHT1 = DHT22 Humidity and Temperature Sensor
  LED1 = RGB LED (com. cathode, rgb) [package="5 mm [THT]"]
  R1 = Resistor [tolerance=±5% power=0.25 resistance=220 package=THT]
  R2 = Resistor [tolerance=±5% power=0.25 resistance=220 package=THT]
  R3 = Resistor [tolerance=±5% power=0.25 resistance=220 package=THT]
  Capacitive_Soil_Moisture_Sensor1 = DFRobot Capacitive Soil Moisture Sensor V1.0 [part_number=SEN0193]

nets:
  N1: U1.D1, OLED1.SCL
  N2: U1.D2, OLED1.SDA
  N3: U1.D3, R1.Pin_1
  N4: U1.D4, R2.Pin_1
  N5: U1.GND, LED1.common_cathode
  N6: U1.D5, DHT1.DATA
  N7: U1.D6, Capacitive_Soil_Moisture_Sensor1.A
  N8: U1.D7, R3.Pin_1
  N9: LED1.red_anode, R1.Pin_0
  N10: LED1.green_anode, R2.Pin_0
  N11: LED1.blue_anode, R3.Pin_0

custom parts:
  NodeMCU V1.0: ESP8266 based NodeMCU
  DFRobot Capacitive Soil Moisture Sensor V1.0: DFRobot Capacitive Soil Moisture Sensor V1.0 This product measures soil moisture levels by capacitive sensing, rather than resistive sensing like other types of moisture sensor. It is made of a corrosion resistant material giving it a long service life. Insert it into soil and impress your friends with the real-time soil moisture data! The product includes an on-board voltage regulator which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
